// Logisim project 1bit_CPU.circ as structural Verilog: 4 circuits, main circuit One_Bit_CPU
module CPU_and_ProgramRom (
);

  wire MasterClock_out, por_1_out;
  wire [7:0] ProgramROM_data;
  wire [10:0] one_bit_cpu_1_dataaddress;
  wire [11:0] one_bit_cpu_1_instructionaddress;

  Clock MasterClock (.out(MasterClock_out));
  POR por_1 (.out(por_1_out));
  ROM #(.addrWidth(12)) ProgramROM (.addr(one_bit_cpu_1_instructionaddress), .data(ProgramROM_data));
  One_Bit_CPU one_bit_cpu_1 (
    .Clock(MasterClock_out), .Reset(por_1_out), .DataIn(one_bit_cpu_1_dataaddress[0]),
    .InstructionIn(ProgramROM_data), .DataAddress(one_bit_cpu_1_dataaddress),
    .InstructionAddress(one_bit_cpu_1_instructionaddress));  // open: DataOut, Write

  // Notes on the sheet:
  //   contents of ProgramROM (hex, n*v repeats v):
  //   8c 60 88 20 61 1 80 1 40 88 41 f0 e 80 62 e0 12 80 63 80 e0 12 80 64
endmodule

module One_Bit_CPU (
  input  Clock,
  input  Reset,
  input  DataIn,
  input  [7:0] InstructionIn,
  output DataOut,
  output Write,
  output [10:0] DataAddress,
  output [11:0] InstructionAddress
);

  wire Accumulator_q, and_1_out, Clk1, Clk2, Clk3, EitherJMP_out, FetchNext_qn, JMPT_out, multiplexer_1_out,
       not_1_out, not_2_out, not_3_out, or_1_out, Registers_dout;
  wire [1:0] counter_1_q;
  wire [2:0] StackPointer_q;
  wire [6:0] FetchNext_q;
  wire [11:0] InstructionRegister_q, multiplexer_2_out, ProgramStack_dout;
  wire [19:0] Microcode_data;

  Counter #(.max('h2), .width(2)) counter_1 (
    .load(1'b0), .count(1'b1), .Q(counter_1_q), .up(1'b1), .clk(Clock), .clr(Reset));  // open: D, carry
  Demultiplexer #(.enable("true"), .select(2)) demultiplexer_1 (
    .out0(Clk1), .out1(Clk2), .out2(Clk3), .in(1'b1), .sel(counter_1_q), .en(not_1_out));  // open: out3
  not not_1 (not_1_out, Reset);
  ROM #(.addrWidth(7), .dataWidth(20)) Microcode (
    .addr({FetchNext_q[6:3], InstructionRegister_q[11:10], FetchNext_q[0]}), .data(Microcode_data));
  Counter #(.max('h7), .width(3)) StackPointer (
    .clr(Reset), .load(Microcode_data[18]), .up(Microcode_data[19]), .count(1'b1), .clk(Clk1),
    .Q(StackPointer_q));  // open: D, carry
  // Probe on Microcode_data
  and and_1 (and_1_out, Registers_dout, Accumulator_q);
  or or_1 (or_1_out, Registers_dout, Accumulator_q);
  not not_2 (not_2_out, Accumulator_q);
  RAM #(.addrWidth(3), .dataWidth(12)) ProgramStack (
    .addr(StackPointer_q), .we(Microcode_data[16]), .oe(Microcode_data[17]), .din(InstructionAddress),
    .dout(ProgramStack_dout));  // open: clk
  Multiplexer #(.select(3)) multiplexer_1 (
    .in0(and_1_out), .in1(or_1_out), .in2(not_2_out), .in3(Registers_dout), .in4(DataIn), .in5(1'b1),
    .in6(1'b0), .out(multiplexer_1_out), .sel(Microcode_data[2:0]));  // open: in7
  T_Flip_Flop FetchNext (
    .T(Microcode_data[15]), .clk(Clk2), .Q(FetchNext_q[0]), .Qn(FetchNext_qn), .reset(Reset));  // open: preset
  Register #(.width(1)) Accumulator (
    .D(multiplexer_1_out), .en(Microcode_data[3]), .clk(Clk3), .Q(Accumulator_q), .clr(Reset));
  Register ExtraByte (.D(InstructionIn), .en(FetchNext_q[0]), .clk(Clk1), .Q(InstructionRegister_q[7:0]), .clr(Reset));
  Register InstructionRegister (
    .D(InstructionIn), .en(FetchNext_qn), .clk(Clk1), .Q({FetchNext_q[6:3], InstructionRegister_q[11:8]}),
    .clr(Reset));
  RAM #(.addrWidth(5), .dataWidth(1)) Registers (
    .addr({FetchNext_q[3], InstructionRegister_q[11:8]}), .we(Microcode_data[4]), .oe(Microcode_data[6]),
    .clk(Clk2), .din(Accumulator_q), .dout(Registers_dout));
  or EitherJMP (EitherJMP_out, Microcode_data[12], JMPT_out);
  Multiplexer #(.width(12)) multiplexer_2 (
    .in0(InstructionRegister_q), .in1(ProgramStack_dout), .out(multiplexer_2_out), .sel(Microcode_data[14]));
  and JMPT (JMPT_out, Microcode_data[11], Accumulator_q);
  Counter #(.max('hfff), .width(12)) ProgramCounter (
    .clr(Reset), .load(EitherJMP_out), .up(not_3_out), .count(1'b1), .clk(Clk2), .D(multiplexer_2_out),
    .Q(InstructionAddress));  // open: carry
  not not_3 (not_3_out, Microcode_data[13]);
  Counter #(.max('h7ff), .width(11)) DataAddressLatch (
    .clr(Reset), .load(Microcode_data[8]), .up(Microcode_data[9]), .count(Microcode_data[10]), .clk(Clk1),
    .D(InstructionRegister_q[10:0]), .Q(DataAddress));  // open: carry
  Register #(.width(1)) DataOutLatch (.D(Accumulator_q), .en(Microcode_data[5]), .clk(Clk2), .Q(DataOut), .clr(Reset));
  Register #(.width(1)) WriteLatch (.D(Microcode_data[6]), .en(Microcode_data[7]), .clk(Clk2), .Q(Write), .clr(Reset));

  // Other names for the same wires on the sheet: Rst = Reset

  // Notes on the sheet:
  //   contents of Microcode (hex, n*v repeats v):
  //   48 0 48 0 48 0 48 0 48 0 48 0 48 0 48 0 49 0 49 0 49 0 49 0 49 0 49 0 49 0 49 0 4b 0 4b 0 4b 0 4b 0
  //   4b 0 4b 0 4b 0 4b 0 10 0 10 0 10 0 10 0 10 0 10 0 10 0 10 0 4a 0 0 0 e 0 d 25*0 8000 810c 8000 810c
  //   8000 81e0 8000 81e0 8*0 8000 8800 8000 8800 8000 8800 8000 8800 8000 9000 8000 9000 8000 9000 8000
  //   9000
endmodule

module RegisterBank8 (
  input  [2:0] Address,
  input  DataIn,
  input  Clk,
  input  Write,
  input  Reset,
  output DataOut
);

  wire and_1_out, d_ff_1_q, d_ff_2_q, d_ff_3_q, d_ff_4_q, d_ff_5_q, d_ff_6_q, d_ff_7_q, d_ff_8_q,
       demultiplexer_1_out0, demultiplexer_1_out1, demultiplexer_1_out2, demultiplexer_1_out3,
       demultiplexer_1_out4, demultiplexer_1_out5, demultiplexer_1_out6, demultiplexer_1_out7;

  and and_1 (and_1_out, Clk, Write);
  Demultiplexer #(.select(3)) demultiplexer_1 (
    .out0(demultiplexer_1_out0), .out1(demultiplexer_1_out1), .out2(demultiplexer_1_out2),
    .out3(demultiplexer_1_out3), .out4(demultiplexer_1_out4), .out5(demultiplexer_1_out5),
    .out6(demultiplexer_1_out6), .out7(demultiplexer_1_out7), .in(and_1_out), .sel(Address));
  D_Flip_Flop d_ff_1 (.D(DataIn), .clk(demultiplexer_1_out0), .Q(d_ff_1_q), .reset(Reset));  // open: Qn, preset
  D_Flip_Flop d_ff_2 (.D(DataIn), .clk(demultiplexer_1_out1), .Q(d_ff_2_q), .reset(Reset));  // open: Qn, preset
  D_Flip_Flop d_ff_3 (.D(DataIn), .clk(demultiplexer_1_out2), .Q(d_ff_3_q), .reset(Reset));  // open: Qn, preset
  D_Flip_Flop d_ff_4 (.D(DataIn), .clk(demultiplexer_1_out3), .Q(d_ff_4_q), .reset(Reset));  // open: Qn, preset
  D_Flip_Flop d_ff_5 (.D(DataIn), .clk(demultiplexer_1_out4), .Q(d_ff_5_q), .reset(Reset));  // open: Qn, preset
  D_Flip_Flop d_ff_6 (.D(DataIn), .clk(demultiplexer_1_out5), .Q(d_ff_6_q), .reset(Reset));  // open: Qn, preset
  D_Flip_Flop d_ff_7 (.D(DataIn), .clk(demultiplexer_1_out6), .Q(d_ff_7_q), .reset(Reset));  // open: Qn, preset
  D_Flip_Flop d_ff_8 (.D(DataIn), .clk(demultiplexer_1_out7), .Q(d_ff_8_q), .reset(Reset));  // open: Qn, preset
  Multiplexer #(.select(3)) multiplexer_1 (
    .in0(d_ff_1_q), .in1(d_ff_2_q), .in2(d_ff_3_q), .in3(d_ff_4_q), .in4(d_ff_5_q), .in5(d_ff_6_q),
    .in6(d_ff_7_q), .in7(d_ff_8_q), .out(DataOut), .sel(Address));
endmodule

module RegisterBank32 (
  input  [4:0] Address,
  input  DataIn,
  input  Write,
  input  Clk,
  input  Reset,
  output DataOut
);

  wire and_1_out, demultiplexer_1_out0, demultiplexer_1_out1, demultiplexer_1_out2, demultiplexer_1_out3,
       Regs0_dataout, Regs1_dataout, Regs2_dataout, Regs3_dataout;

  and and_1 (and_1_out, Write, Clk);
  Demultiplexer #(.select(2)) demultiplexer_1 (
    .out0(demultiplexer_1_out0), .out1(demultiplexer_1_out1), .out2(demultiplexer_1_out2),
    .out3(demultiplexer_1_out3), .in(and_1_out), .sel(Address[4:3]));
  RegisterBank8 Regs0 (
    .Address(Address[2:0]), .DataIn(DataIn), .Clk(demultiplexer_1_out0), .Write(Write), .Reset(Reset),
    .DataOut(Regs0_dataout));
  RegisterBank8 Regs1 (
    .Address(Address[2:0]), .DataIn(DataIn), .Clk(demultiplexer_1_out1), .Write(Write), .Reset(Reset),
    .DataOut(Regs1_dataout));
  RegisterBank8 Regs2 (
    .Address(Address[2:0]), .DataIn(DataIn), .Clk(demultiplexer_1_out2), .Write(Write), .Reset(Reset),
    .DataOut(Regs2_dataout));
  RegisterBank8 Regs3 (
    .Address(Address[2:0]), .DataIn(DataIn), .Clk(demultiplexer_1_out3), .Write(Write), .Reset(Reset),
    .DataOut(Regs3_dataout));
  Multiplexer #(.select(2)) multiplexer_1 (
    .in0(Regs0_dataout), .in1(Regs1_dataout), .in2(Regs2_dataout), .in3(Regs3_dataout), .out(DataOut),
    .sel(Address[4:3]));
endmodule
