// Logisim project ALU2_latched.circ as structural Verilog: 1 circuit, main circuit ALU2_latched
module ALU2_latched (
  input  OP_A,
  input  OP_B,
  input  A,
  output ALU_out
);

  wire and_1_out, and_2_out, and_3_out, and_4_out, clock_1_out, d_ff_1_qn, not_1_out, not_2_out, not_3_out,
       or_1_out;

  not not_1 (not_1_out, A);
  not not_2 (not_2_out, OP_A);
  not not_3 (not_3_out, OP_B);
  and and_1 (and_1_out, not_2_out, d_ff_1_qn, OP_B);
  and and_2 (and_2_out, not_1_out, OP_A, ALU_out);
  and and_3 (and_3_out, A, ALU_out, not_3_out);
  and and_4 (and_4_out, A, OP_A, d_ff_1_qn);
  or or_1 (or_1_out, and_1_out, and_2_out, and_3_out, and_4_out);
  Clock clock_1 (.out(clock_1_out));
  D_Flip_Flop d_ff_1 (.D(or_1_out), .clk(clock_1_out), .Q(ALU_out), .Qn(d_ff_1_qn));  // open: preset, reset

  // Notes on the sheet:
  //   OP_A OP_B Oper
  //   0    0     AND
  //   0    1    NOT B
  //   1    0     OR
  //   1    1    XOR
endmodule
