// Logisim project ALU_Latched.circ as structural Verilog: 2 circuits, main circuit ALU
module ALU (
  input  Op_A,
  input  Op_B,
  input  A,
  input  Clock,
  output ALU_Out
);

  wire and_1_out, and_2_out, and_3_out, and_4_out, and_5_out, d_ff_1_qn, not_1_out, not_2_out, or_1_out,
       or_2_out;

  and and_1 (and_1_out, A, ALU_Out);
  or or_1 (or_1_out, A, ALU_Out);
  not not_1 (not_1_out, Op_B);
  not not_2 (not_2_out, Op_A);
  and and_2 (and_2_out, not_2_out, not_1_out, A);
  and and_3 (and_3_out, not_2_out, Op_B, and_1_out);
  and and_4 (and_4_out, Op_A, not_1_out, or_1_out);
  and and_5 (and_5_out, Op_A, Op_B, d_ff_1_qn);
  or or_2 (or_2_out, and_2_out, and_3_out, and_4_out, and_5_out);
  D_Flip_Flop d_ff_1 (.D(or_2_out), .clk(Clock), .Q(ALU_Out), .Qn(d_ff_1_qn));  // open: preset, reset

  // Notes on the sheet:
  //   0 0 LOAD
  //   0 1 AND
  //   1 0 OR
  //   1 1 NOT
endmodule

module CPU (
  input  in_1,
  input  in_2,
  input  in_3,
  output out_4
);

  wire clock_1_out;

  Clock clock_1 (.out(clock_1_out));
  ALU alu_1 (.Op_A(in_1), .Op_B(in_2), .A(in_3), .Clock(clock_1_out), .ALU_Out(out_4));
endmodule
