// Logisim project InstructionDecoder.circ as structural Verilog: 3 circuits, main circuit main
module main (
);

  opcode2microcode opcode2microcode_1 ();  // open: b7, b6, b5, b4, b3, b2, extra, m_20, m_19, m_18, m_17, m_16, m_15, m_14, m_13, m_12, m_11, m_10, m_9, m_8, m_7, m_6, m_5, m_4, m_3, m_2, m_1
endmodule

module opcode2instr (
  input  b7,
  input  b6,
  input  b5,
  input  b4,
  input  b3,
  input  b2,
  output c_and,
  output c_or,
  output c_load,
  output c_save,
  output c_not,
  output c_zero,
  output c_one,
  output c_ret,
  output c_out,
  output c_outinc,
  output c_outdec,
  output c_in,
  output c_ininc,
  output c_indec,
  output c_infrom,
  output c_outto,
  output c_call,
  output c_jmpt,
  output c_jmp
);

  wire not_1_out, not_2_out, not_3_out, not_4_out, not_5_out, not_6_out;

  not not_1 (not_1_out, b7);
  not not_2 (not_2_out, b6);
  not not_3 (not_3_out, b5);
  not not_4 (not_4_out, b4);
  not not_5 (not_5_out, b3);
  not not_6 (not_6_out, b2);
  and and_1 (c_and, not_1_out, not_2_out, not_3_out);
  and and_2 (c_or, not_1_out, not_2_out, b5);
  and and_3 (c_load, not_1_out, b6, not_3_out);
  and and_4 (c_save, not_1_out, b6, b5);
  and and_5 (c_not, b7, not_2_out, not_3_out, not_4_out, not_5_out, not_6_out);
  and and_6 (c_zero, b7, not_2_out, not_3_out, not_4_out, b3, not_6_out);
  and and_7 (c_one, b7, not_2_out, not_3_out, not_4_out, b3, b2);
  and and_8 (c_ret, b7, not_2_out, not_3_out, b4, not_5_out, not_6_out);
  and and_9 (c_out, b7, not_2_out, b5, not_4_out, not_5_out, not_6_out);
  and and_10 (c_outinc, b7, not_2_out, b5, not_4_out, b3, not_6_out);
  and and_11 (c_outdec, b7, not_2_out, b5, not_4_out, b3, b2);
  and and_12 (c_in, b7, not_2_out, b5, b4, not_5_out, not_6_out);
  and and_13 (c_ininc, b7, not_2_out, b5, b4, b3, not_6_out);
  and and_14 (c_indec, b7, not_2_out, b5, b4, b3, b2);
  and and_15 (c_infrom, b7, b6, not_3_out, not_4_out, not_5_out);
  and and_16 (c_outto, b7, b6, not_3_out, not_4_out, b3);
  and and_17 (c_call, b7, b6, not_3_out, b4);
  and and_18 (c_jmpt, b7, b6, b5, not_4_out);
  and and_19 (c_jmp, b7, b6, b5, b4);
endmodule

module opcode2microcode (
  input  b7,
  input  b6,
  input  b5,
  input  b4,
  input  b3,
  input  b2,
  input  extra,
  output m_20,
  output m_19,
  output m_18,
  output m_17,
  output m_16,
  output m_15,
  output m_14,
  output m_13,
  output m_12,
  output m_11,
  output m_10,
  output m_9,
  output m_8,
  output m_7,
  output m_6,
  output m_5,
  output m_4,
  output m_3,
  output m_2,
  output m_1
);

  wire and_1_out, and_2_out, and_7_out, and_8_out, and_9_out, and_10_out, and_13_out, and_14_out, and_15_out,
       and_16_out, and_17_out, and_18_out, and_19_out, and_20_out, and_21_out, and_22_out, and_23_out,
       and_24_out, not_1_out, not_2_out, not_3_out, not_4_out, not_5_out, not_6_out, not_7_out;

  not not_1 (not_1_out, b7);
  not not_2 (not_2_out, b6);
  not not_3 (not_3_out, b5);
  not not_4 (not_4_out, b4);
  not not_5 (not_5_out, b3);
  not not_6 (not_6_out, b2);
  not not_7 (not_7_out, extra);
  and and_1 (and_1_out, b7, b6, not_4_out);
  and and_2 (and_2_out, b7, b6, b5);
  and and_3 (m_13, b7, b6, b5, b4, extra);
  and and_4 (m_12, b7, b6, b5, not_4_out, extra);
  and and_5 (m_9, b7, b6, not_3_out, not_4_out, extra);
  and and_6 (m_8, b7, b6, not_3_out, not_4_out, b3, extra);
  and and_7 (and_7_out, not_2_out, not_3_out, not_4_out, not_5_out, not_6_out, not_7_out);
  and and_8 (and_8_out, not_1_out, not_2_out, not_7_out);
  and and_9 (and_9_out, not_1_out, not_3_out, not_7_out);
  and and_10 (and_10_out, b7, b6, not_3_out, not_4_out, b3, extra);
  and and_11 (m_6, b7, b6, not_3_out, not_4_out, b3, extra);
  and and_12 (m_5, not_1_out, b6, b5, not_7_out);
  and and_13 (and_13_out, not_2_out, not_3_out, not_4_out, not_6_out, not_7_out);
  and and_14 (and_14_out, not_2_out, not_3_out, not_4_out, b3, not_7_out);
  and and_15 (and_15_out, not_1_out, not_2_out, not_7_out);
  and and_16 (and_16_out, not_1_out, not_3_out, not_7_out);
  and and_17 (and_17_out, b7, b6, not_3_out, not_4_out, not_5_out, extra);
  and and_18 (and_18_out, b7, b6, not_3_out, not_4_out, not_5_out, extra);
  and and_19 (and_19_out, b7, not_2_out, not_3_out, not_4_out, b3, not_7_out);
  and and_20 (and_20_out, not_1_out, b6, not_3_out, not_7_out);
  and and_21 (and_21_out, b7, not_2_out, not_3_out, not_4_out, not_6_out, not_7_out);
  and and_22 (and_22_out, not_1_out, b6, not_3_out, not_7_out);
  and and_23 (and_23_out, b7, not_2_out, not_3_out, not_4_out, b3, b2, not_7_out);
  and and_24 (and_24_out, not_1_out, not_2_out, b5, not_7_out);
  or or_1 (m_16, and_1_out, and_2_out);
  or or_2 (m_7, and_7_out, and_8_out, and_9_out, and_10_out);
  or or_3 (m_4, and_13_out, and_14_out, and_15_out, and_16_out, and_17_out);
  or or_4 (m_3, and_18_out, and_19_out);
  or or_5 (m_2, and_20_out, and_21_out);
  or or_6 (m_1, and_22_out, and_23_out, and_24_out);

  assign m_10 = 1'b0;
  assign m_11 = 1'b0;
  assign m_14 = 1'b0;
  assign m_15 = 1'b0;
  assign m_17 = 1'b0;
  assign m_18 = 1'b0;
  assign m_19 = 1'b0;
  assign m_20 = 1'b0;
endmodule
