// Logisim project 1bit_CPU.circ as structural Verilog: 4 circuits, main circuit One_Bit_CPU
module CPU_and_ProgramRom (
);

  wire MasterClock_out, por_1_out;
  wire [7:0] ProgramROM_data;
  wire [10:0] one_bit_cpu_1_dataaddress;
  wire [11:0] one_bit_cpu_1_instructionaddress;

  Clock MasterClock (.out(MasterClock_out));
  POR por_1 (.out(por_1_out));
  ROM #(.addrWidth(12)) ProgramROM (.addr(one_bit_cpu_1_instructionaddress), .data(ProgramROM_data));
  One_Bit_CPU one_bit_cpu_1 (
    .DataIn(one_bit_cpu_1_dataaddress[0]), .InstructionIn(ProgramROM_data), .Clock(MasterClock_out),
    .Reset(por_1_out), .DataAddress(one_bit_cpu_1_dataaddress),
    .InstructionAddress(one_bit_cpu_1_instructionaddress));  // open: DataOut, Write, Read

  // Notes on the sheet:
  //   contents of ProgramROM (hex, n*v repeats v):
  //   8c c8 0 d0 9 d0 c f0 12 a0 90 94 d0 10 90 94 90 94 98
endmodule

module One_Bit_CPU (
  input  DataIn,
  input  [7:0] InstructionIn,
  input  Clock,
  input  Reset,
  output DataOut,
  output Write,
  output Read,
  output [10:0] DataAddress,
  output [11:0] InstructionAddress
);

  wire Accumulator_q, and_1_out, Clk0, Clk1, Clk2, EitherJMP_out, FetchNext_qn, JMPT_out, multiplexer_1_out,
       not_1_out, not_2_out, or_1_out, or_2_out, PCOV, Registers_dout, StackOV;
  wire [6:0] FetchNext_q;
  wire [11:0] multiplexer_2_out, stack_1_dataout;
  wire [11:8] InstructionRegister_q;
  wire [19:0] Microcode_data;

  ROM #(.addrWidth(7), .dataWidth(20)) Microcode (
    .addr({FetchNext_q[6:3], InstructionRegister_q[11:10], FetchNext_q[0]}),
    .data({Microcode_data[19:9], Read, Microcode_data[7:0]}));
  or or_1 (or_1_out, Microcode_data[19], PCOV, StackOV);
  Clock_Gen clock_gen_1 (.Clock(Clock), .Halt(or_1_out), .Reset(Reset), .Clk0(Clk0), .Clk1(Clk1), .Clk2(Clk2));
  and and_1 (and_1_out, Registers_dout, Accumulator_q);
  or or_2 (or_2_out, Registers_dout, Accumulator_q);
  not not_1 (not_1_out, Accumulator_q);
  Multiplexer #(.select(3)) multiplexer_1 (
    .in0(1'b0), .in1(1'b1), .in2(Registers_dout), .in3(and_1_out), .in4(or_2_out), .in5(not_1_out),
    .in6(DataIn), .out(multiplexer_1_out), .sel(Microcode_data[2:0]));  // open: in7
  Register #(.width(1)) Accumulator (
    .D(multiplexer_1_out), .en(Microcode_data[3]), .clk(Clk2), .Q(Accumulator_q), .clr(Reset));
  T_Flip_Flop FetchNext (
    .T(Microcode_data[16]), .clk(Clk1), .Q(FetchNext_q[0]), .Qn(FetchNext_qn), .reset(Reset));  // open: preset
  Register InstructionRegister (
    .D(InstructionIn), .en(FetchNext_qn), .clk(Clk0), .Q({FetchNext_q[6:3], InstructionRegister_q}),
    .clr(Reset));
  Stack stack_1 (
    .DataIn(InstructionAddress), .Push(Microcode_data[17]), .Clock(Clk2), .Enable(Microcode_data[18]),
    .Reset(Reset), .DataOut(stack_1_dataout), .Overflow(StackOV));
  RAM #(.addrWidth(5), .dataWidth(1)) Registers (
    .addr({FetchNext_q[3], InstructionRegister_q}), .we(Microcode_data[4]), .oe(Microcode_data[5]),
    .clk(Clk1), .din(Accumulator_q), .dout(Registers_dout));
  or EitherJMP (EitherJMP_out, Microcode_data[13], JMPT_out);
  Multiplexer #(.width(12)) multiplexer_2 (
    .in0({InstructionRegister_q, InstructionIn}), .in1(stack_1_dataout), .out(multiplexer_2_out),
    .sel(Microcode_data[15]));
  and JMPT (JMPT_out, Microcode_data[12], Accumulator_q);
  not not_2 (not_2_out, Microcode_data[14]);
  Counter #(.max('h7ff), .ongoal("stay"), .width(11)) DataAddressLatch (
    .clr(Reset), .load(Microcode_data[9]), .up(Microcode_data[10]), .count(Microcode_data[11]), .clk(Clk1),
    .D({InstructionRegister_q[10:8], InstructionIn}), .Q(DataAddress));  // open: carry
  Counter #(.max('hfff), .ongoal("stay"), .width(12)) ProgramCounter (
    .clr(Reset), .load(EitherJMP_out), .up(not_2_out), .count(1'b1), .clk(Clk0), .D(multiplexer_2_out),
    .carry(PCOV), .Q(InstructionAddress));
  and and_2 (DataOut, Accumulator_q, Microcode_data[6]);
  and and_3 (Write, Microcode_data[7], Clk2);

  // Other names for the same wires on the sheet: Rst = Reset

  // Notes on the sheet:
  //   contents of Microcode (hex, n*v repeats v):
  //   2b 3 2b 3 2b 3 2b 3 2b 3 2b 3 2b 3 2b 3 2c 4 2c 4 2c 4 2c 4 2c 4 2c 4 2c 4 2c 4 2a 0 2a 0 2a 0 2a 0
  //   2a 0 2a 0 2a 0 2a 0 10 0 10 0 10 0 10 0 10 0 10 0 10 0 10 0 2d 0 0 0 8 0 9 0 a000 0 40000 0 80000 0
  //   0 0 c0 0 0 0 cc0 0 8c0 0 10e 0 0 0 d0e 0 90e 0 10a00 1010e 10a00 1010e 10a00 100c0 10a00 100c0 10000
  //   72000 10000 72000 10000 72000 10000 72000 10000 11000 10000 11000 10000 11000 10000 11000 10000
  //   12000 10000 12000 10000 12000 10000 12000
endmodule

module Clock_Gen (
  input  Clock,
  input  Halt,
  input  Reset,
  output Clk0,
  output Clk1,
  output Clk2
);

  wire and_1_out;

  and and_1 (and_1_out, Clock, ~Halt);  // AND_Gate
  D_Flip_Flop d_ff_1 (.clk(and_1_out), .D(Clk2), .Q(Clk0), .preset(Reset));  // open: Qn, reset
  D_Flip_Flop d_ff_2 (.clk(and_1_out), .D(Clk0), .Q(Clk1), .reset(Reset));  // open: Qn, preset
  D_Flip_Flop d_ff_3 (.clk(and_1_out), .D(Clk1), .Q(Clk2), .reset(Reset));  // open: Qn, preset
endmodule

module Stack (
  input  [11:0] DataIn,
  input  Push,
  input  Clock,
  input  Enable,
  input  Reset,
  output Overflow,
  output [11:0] DataOut
);

  wire and_1_out, and_2_out, d_ff_1_q, or_1_out;
  wire [11:0] multiplexer_1_out, multiplexer_2_out, multiplexer_3_out, multiplexer_4_out, multiplexer_5_out,
       multiplexer_6_out, multiplexer_7_out, register_1_q, register_2_q, register_3_q, register_4_q,
       register_5_q, register_6_q, register_7_q;

  Multiplexer #(.width(12)) multiplexer_1 (.in0(register_1_q), .in1(DataIn), .out(multiplexer_1_out), .sel(Push));
  Counter #(.max('hfff), .width(12)) counter_1 (
    .load(Enable), .D(multiplexer_1_out), .count(and_2_out), .Q(DataOut), .up(1'b1), .clk(Clock), .clr(Reset));  // open: carry
  D_Flip_Flop d_ff_1 (.D(Push), .clk(Clock), .Q(d_ff_1_q), .reset(Reset));  // open: Qn, preset
  Register #(.width(12)) register_1 (
    .D(multiplexer_2_out), .clk(and_1_out), .Q(register_1_q), .clr(Reset));  // open: en
  Multiplexer #(.width(12)) multiplexer_2 (.in0(multiplexer_3_out), .in1(DataOut), .out(multiplexer_2_out), .sel(Push));
  and and_1 (and_1_out, Clock, Enable);
  and and_2 (and_2_out, ~Enable, ~Push, d_ff_1_q);  // AND_Gate
  Register #(.width(12)) register_2 (
    .D(multiplexer_3_out), .clk(and_1_out), .Q(register_2_q), .clr(Reset));  // open: en
  Multiplexer #(.width(12)) multiplexer_3 (.in0(register_3_q), .in1(register_1_q), .out(multiplexer_3_out), .sel(Push));
  Register #(.width(12)) register_3 (
    .D(multiplexer_4_out), .clk(and_1_out), .Q(register_3_q), .clr(Reset));  // open: en
  Multiplexer #(.width(12)) multiplexer_4 (
    .in0(multiplexer_5_out), .in1(register_2_q), .out(multiplexer_4_out), .sel(Push));
  Multiplexer #(.width(12)) multiplexer_5 (.in0(register_5_q), .in1(register_3_q), .out(multiplexer_5_out), .sel(Push));
  Register #(.width(12)) register_4 (
    .D(multiplexer_5_out), .clk(and_1_out), .Q(register_4_q), .clr(Reset));  // open: en
  Register #(.width(12)) register_5 (
    .D(multiplexer_6_out), .clk(and_1_out), .Q(register_5_q), .clr(Reset));  // open: en
  Multiplexer #(.width(12)) multiplexer_6 (
    .in0(multiplexer_7_out), .in1(register_4_q), .out(multiplexer_6_out), .sel(Push));
  Register #(.width(12)) register_6 (
    .D(multiplexer_7_out), .clk(and_1_out), .Q(register_6_q), .clr(Reset));  // open: en
  Multiplexer #(.width(12)) multiplexer_7 (.in0(register_7_q), .in1(register_5_q), .out(multiplexer_7_out), .sel(Push));
  Register #(.width(12)) register_7 (.D(register_6_q), .clk(and_1_out), .Q(register_7_q), .clr(Reset));  // open: en
  or or_1 (or_1_out, register_7_q[0], register_7_q[1], register_7_q[2], register_7_q[3], register_7_q[4], register_7_q[5], register_7_q[6], register_7_q[7], register_7_q[8], register_7_q[9], register_7_q[10], register_7_q[11]);
  and and_3 (Overflow, or_1_out, Push, and_1_out);

  // Notes on the sheet:
  //   This part of the circuit automaticall increments the address pushed into the stack by a CALL instruction
  //   The first stage of the stack is not a simple D-Flip Flop but a counter.
  //   The reason is that the stack should store the return address for the RET instruction.
  //   At the time of PUSHing, the second byte of the CALL is what is available so it needs to be incremented to point to the next address.
endmodule
