// Digital circuit CTL-test.dig as structural Verilog
module CTL_test (
  input  [3:0] I,
  input  RST,
  output SetRR,
  output NotOut,
  output Write,
  output SetIEN,
  output SetOEN,
  output JMP,
  output RTN,
  output Skip,
  output FLG0,
  output FLGF
);

  CTL ctl_1 (
    .SetRR(SetRR), .NotOut(NotOut), .Write(Write), .SetIEN(SetIEN), .SetOEN(SetOEN), .JMP(JMP), .RTN(RTN),
    .Skip(Skip), .FLG0(FLG0), .FLGF(FLGF), .I(I), .RST(RST));
endmodule

/* Test case:
           RST  I SetRR NotOut Write SetIEN SetOEN JMP RTN Skip FLG0 FLGF
# Reset
repeat(16)  1  (n)  x     x      x     x       x    0   0    0   0    0

# NOP0
            0   0   0     0      0     0       0    0   0    0   1    0

# LD
            0   1   1     x      0     0       0    0   0    0   0    0

# LDC
            0   2   1     x      0     0       0    0   0    0   0    0

# AND
            0   3   1     x      0     0       0    0   0    0   0    0

# ANDC
            0   4   1     x      0     0       0    0   0    0   0    0

# OR
            0   5   1     x      0     0       0    0   0    0   0    0

# ORC
            0   6   1     x      0     0       0    0   0    0   0    0

# XNOR
            0   7   1     x      0     0       0    0   0    0   0    0

# STO
            0   8   0     0      1     0       0    0   0    0   0    0

# STOC
            0   9   0     1      1     0       0    0   0    0   0    0

# IEN
            0   0xa 0     x      0     1       0    0   0    0   0    0

# OEN
            0   0xb 0     x      0     0       1    0   0    0   0    0

# JMP
            0   0xc 0     x      0     0       0    1   0    0   0    0

# RTN
            0   0xd 0     x      0     0       0    0   1    1   0    0

# SKP
            0   0xe 0     x      0     0       0    0   0    1   0    0

# NOPF
            0   0xf 0     x      0     0       0    0   0    0   0    1
*/
