// Digital circuit CTL.dig as structural Verilog
module CTL (
  input  [3:0] I,
  input  RST,
  output SetRR,
  output NotOut,
  output Write,
  output SetIEN,
  output SetOEN,
  output JMP,
  output RTN,
  output Skip,
  output FLG0,
  output FLGF
);

  wire and_1_out, and_2_out, and_3_out, and_9_out, and_10_out, not_1_out, not_2_out, not_3_out, not_4_out,
       not_5_out;

  not not_1 (not_1_out, RST);
  not not_2 (not_2_out, I[3]);
  not not_3 (not_3_out, I[2]);
  not not_4 (not_4_out, I[1]);
  not not_5 (not_5_out, I[0]);
  and and_1 (and_1_out, I[0], not_2_out);
  and and_2 (and_2_out, I[1], not_2_out);
  and and_3 (and_3_out, I[2], not_2_out);
  and and_4 (Write, not_4_out, not_3_out, I[3]);
  and and_5 (SetIEN, not_5_out, I[1], not_3_out, I[3]);
  and and_6 (SetOEN, I[0], I[1], not_3_out, I[3]);
  and and_7 (JMP, not_5_out, not_4_out, I[2], I[3], not_1_out);
  and and_8 (RTN, I[0], not_4_out, I[2], I[3], not_1_out);
  and and_9 (and_9_out, I[0], not_4_out, I[2], I[3], not_1_out);
  and and_10 (and_10_out, not_5_out, I[1], I[2], I[3], not_1_out);
  and and_11 (FLG0, not_5_out, not_4_out, not_3_out, not_2_out, not_1_out);
  and and_12 (FLGF, I[0], I[1], I[2], I[3], not_1_out);
  or or_1 (SetRR, and_1_out, and_2_out, and_3_out);
  or or_2 (Skip, and_9_out, and_10_out);

  assign NotOut = I[0];
endmodule
