// Digital circuit ClkGen.dig as structural Verilog
// Two phase clock generator
module ClkGen (
  input  ClkIn,
  input  Reset,
  output T0,
  output T1
);

  wire d_ff_as_2_q, d_ff_as_4_q;

  D_FF_AS d_ff_as_1 (.Set(Reset), .D(d_ff_as_4_q), .C(ClkIn), .Clr(1'b0), .Q(T0));  // open: nQ
  D_FF_AS d_ff_as_2 (.Set(1'b0), .D(T0), .C(ClkIn), .Clr(Reset), .Q(d_ff_as_2_q));  // open: nQ
  D_FF_AS d_ff_as_3 (.Set(1'b0), .D(d_ff_as_2_q), .C(ClkIn), .Clr(Reset), .Q(T1));  // open: nQ
  D_FF_AS d_ff_as_4 (.Set(1'b0), .D(T1), .C(ClkIn), .Clr(Reset), .Q(d_ff_as_4_q));  // open: nQ
endmodule
