// Digital circuit ClkGen1.dig as structural Verilog
// Two phase clock generator
module ClkGen1 (
  input  Reset,
  input  ClkIn,
  output T0,
  output T1
);

  wire delay_1_out, delay_2_out, not_1_out, or_1_out;

  or or_1 (or_1_out, ClkIn, Reset);
  not not_1 (not_1_out, or_1_out);
  Delay #(.delayTime(2)) delay_1 (.in(or_1_out), .out(delay_1_out));
  Delay delay_2 (.in(not_1_out), .out(delay_2_out));
  RS_FF_AS rs_ff_as_1 (.S(delay_1_out), .R(not_1_out), .Q(T0));  // open: nQ
  RS_FF_AS rs_ff_as_2 (.S(delay_2_out), .R(or_1_out), .Q(T1));  // open: nQ
endmodule
