// Digital circuit ICU.dig as structural Verilog
module ICU (
  input  clk,
  input  I1,
  input  I2,
  input  I3,
  input  I4,
  input  I5,
  input  I6,
  input  I7
);

  wire and_1_out, mc14500_1_flg0, mc14500_1_flgf, mc14500_1_jmp, mc14500_1_rr, mc14500_1_rtn,
       mc14500_1_write, mc14500_1_x1, mc14512_1_z, mc14599_1_q0, mc14599_1_q1, mc14599_1_q2, mc14599_1_q3,
       mc14599_1_q4, mc14599_1_q5, mc14599_1_q6, mc14599_1_q7, mc14599_2_q0, mc14599_2_q1, mc14599_2_q2,
       mc14599_2_q3, mc14599_2_q4, mc14599_2_q5, mc14599_2_q6, mc14599_2_q7, not_1_out, not_2_out, or_1_out,
       or_2_out, or_3_out, reset_1_out;
  wire [3:0] counter_1_out, counter_1_out_2, rom_1_d, rom_1_d_2;

  or or_1 (or_1_out, clk, mc14500_1_flgf);
  or or_2 (or_2_out, mc14500_1_flg0, reset_1_out);
  Reset reset_1 (.out(reset_1_out));
  not not_1 (not_1_out, mc14500_1_x1);
  Seven_Seg_Hex seven_seg_hex_1 (.d(counter_1_out_2), .dp(1'b0));
  Counter #(.Bits(8)) counter_1 (
    .en(1'b1), .C(not_1_out), .clr(or_2_out), .out({counter_1_out_2, counter_1_out}));  // open: ovf
  Seven_Seg_Hex seven_seg_hex_2 (.d(counter_1_out), .dp(1'b0));
  Seven_Seg_Hex seven_seg_hex_3 (.d(rom_1_d_2), .dp(1'b0));
  ROM #(.AddrBits(8), .Bits(8)) rom_1 (.A({counter_1_out_2, counter_1_out}), .sel(1'b1), .D({rom_1_d_2, rom_1_d}));
  Seven_Seg_Hex seven_seg_hex_4 (.d(rom_1_d), .dp(1'b0));
  MC14500 mc14500_1 (
    .Data(mc14512_1_z), .I(rom_1_d_2), .X2(or_1_out), .RST(or_2_out), .Write(mc14500_1_write),
    .RR(mc14500_1_rr), .JMP(mc14500_1_jmp), .RTN(mc14500_1_rtn), .FLG0(mc14500_1_flg0),
    .FLGF(mc14500_1_flgf), .X1(mc14500_1_x1));
  LED JMP (.in(mc14500_1_jmp));
  LED RTN (.in(mc14500_1_rtn));
  LED FLG0 (.in(mc14500_1_flg0));
  LED FLGF (.in(mc14500_1_flgf));
  LED RR (.in(mc14500_1_rr));
  LED Data (.in(mc14512_1_z));
  LED Clk_X1 (.in(mc14500_1_x1));
  LED Write (.in(mc14500_1_write));
  or or_3 (or_3_out, rom_1_d[3], mc14500_1_x1, mc14500_1_write);
  and and_1 (and_1_out, not_2_out, mc14500_1_write);
  not not_2 (not_2_out, rom_1_d[3]);
  MC14512 mc14512_1 (
    .A(rom_1_d[0]), .B(rom_1_d[1]), .C(rom_1_d[2]), .INH(1'b0), .DIS(or_3_out), .Z(mc14512_1_z),
    .X0(mc14500_1_rr), .X1(I1), .X2(I2), .X3(I3), .X4(I4), .X5(I5), .X6(I6), .X7(I7));
  MC14599 mc14599_1 (
    .Data(mc14512_1_z), .RESET(or_2_out), .Q7(mc14599_1_q7), .Q6(mc14599_1_q6), .Q5(mc14599_1_q5),
    .Q4(mc14599_1_q4), .Q3(mc14599_1_q3), .Q2(mc14599_1_q2), .Q1(mc14599_1_q1), .Q0(mc14599_1_q0),
    .A0(rom_1_d[0]), .A1(rom_1_d[1]), .A2(rom_1_d[2]), .Enable(and_1_out), .Write(mc14500_1_write),
    .WriteDisable(mc14500_1_x1));
  MC14599 mc14599_2 (
    .Data(mc14512_1_z), .RESET(or_2_out), .Q7(mc14599_2_q7), .Q6(mc14599_2_q6), .Q5(mc14599_2_q5),
    .Q4(mc14599_2_q4), .Q3(mc14599_2_q3), .Q2(mc14599_2_q2), .Q1(mc14599_2_q1), .Q0(mc14599_2_q0),
    .A0(rom_1_d[0]), .A1(rom_1_d[1]), .A2(rom_1_d[2]), .Enable(rom_1_d[3]), .Write(mc14500_1_write),
    .WriteDisable(mc14500_1_x1));
  LED O0 (.in(mc14599_1_q0));
  LED O1 (.in(mc14599_1_q1));
  LED O2 (.in(mc14599_1_q2));
  LED O3 (.in(mc14599_1_q3));
  LED O4 (.in(mc14599_1_q4));
  LED O5 (.in(mc14599_1_q5));
  LED O6 (.in(mc14599_1_q6));
  LED O7 (.in(mc14599_1_q7));
  LED O8 (.in(mc14599_2_q0));
  LED O9 (.in(mc14599_2_q1));
  LED O10 (.in(mc14599_2_q2));
  LED O11 (.in(mc14599_2_q3));
  LED O12 (.in(mc14599_2_q4));
  LED O13 (.in(mc14599_2_q5));
  LED O14 (.in(mc14599_2_q6));
  LED O15 (.in(mc14599_2_q7));

  // Notes on the sheet:
  //   Program
  //   Counter
  //   Program
  //   Address
  //   Program
  //   Memory
  //   contents of rom_1 (hex, n*v repeats v):
  //   0,1,2,3
  //   Instruction
  //   IO Address
endmodule
