// Digital circuit LU.dig as structural Verilog
module LU (
  input  RR,
  input  DIn,
  input  [3:0] I,
  output NewRR
);

  wire and_1_out, and_2_out, and_3_out, and_4_out, and_5_out, and_6_out, not_1_out, not_2_out, not_3_out,
       not_4_out, not_5_out;

  not not_1 (not_1_out, I[2]);
  not not_2 (not_2_out, I[1]);
  not not_3 (not_3_out, I[0]);
  not not_4 (not_4_out, RR);
  not not_5 (not_5_out, DIn);
  and and_1 (and_1_out, DIn, I[0], not_1_out, RR);
  and and_2 (and_2_out, DIn, I[0], I[2], not_4_out);
  and and_3 (and_3_out, not_5_out, I[2], RR);
  and and_4 (and_4_out, DIn, I[0], not_2_out);
  and and_5 (and_5_out, not_5_out, not_3_out, I[1]);
  and and_6 (and_6_out, not_3_out, I[1], I[2], RR);
  or or_1 (NewRR, and_1_out, and_2_out, and_3_out, and_4_out, and_5_out, and_6_out);
  // Pins of 3 and 4 bits meet at I
endmodule
