// Digital circuit MC14500.dig as structural Verilog
module MC14500 (
  input  [3:0] I,
  input  Data,
  input  X2,
  input  RST,
  output FLG0,
  output FLGF,
  output X1,
  output Write,
  output RTN,
  output JMP,
  output RR
);

  wire and_1_out, and_2_out, and_3_out, and_4_out, and_5_out, ctl_1_notout, ctl_1_setien, ctl_1_setoen,
       ctl_1_setrr, ctl_1_skip, ctl_1_write, IEN_nq, LU_p3, OEN_nq, or_1_out, Skip_nq, T0, T1, xor_1_out;
  wire [3:0] Instruction_Register_q;

  or or_1 (or_1_out, RST, and_1_out);
  ClkGen1 clkgen1_1 (.T0(T0), .T1(T1), .ClkIn(X2), .Reset(RST));
  and and_1 (and_1_out, T0, Skip_nq);
  Register #(.Bits(4)) Instruction_Register (.D(I), .C(or_1_out), .en(1'b1), .Q(Instruction_Register_q));
  T_FF Skip (.T(ctl_1_skip), .C(T0), .nQ(Skip_nq));  // open: Q
  CTL ctl_1 (
    .SetRR(ctl_1_setrr), .NotOut(ctl_1_notout), .Write(ctl_1_write), .SetIEN(ctl_1_setien),
    .SetOEN(ctl_1_setoen), .JMP(JMP), .RTN(RTN), .Skip(ctl_1_skip), .FLG0(FLG0), .FLGF(FLGF),
    .I(Instruction_Register_q), .RST(RST));
  D_FF_AS IEN (.Set(1'b0), .D(Data), .C(ctl_1_setien), .Clr(RST), .nQ(IEN_nq));  // open: Q
  and and_2 (and_2_out, Data, IEN_nq);
  and and_3 (and_3_out, T0, ctl_1_setrr);
  // LU LU: pin names not known; wires that end beside it: and_2_out, Instruction_Register_q, LU_p3, RR
  assign Data = and_4_out ? xor_1_out : 1'bz;  // Driver driver_1
  D_FF_AS u_RR (.Set(1'b0), .D(LU_p3), .C(and_3_out), .Clr(RST), .Q(RR));  // open: nQ
  xor xor_1 (xor_1_out, RR, ctl_1_notout);
  and and_4 (and_4_out, ctl_1_write, T1);
  D_FF_AS OEN (.Set(1'b0), .D(xor_1_out), .C(and_5_out), .Clr(RST), .nQ(OEN_nq));  // open: Q
  and and_5 (and_5_out, T1, ctl_1_setoen);
  and and_6 (Write, OEN_nq, and_4_out);
  not not_1 (X1, T1);

  // Notes on the sheet:
  //   I: pin 7,6,5,4
  //   FLG0: pin 10
  //   FLGF: pin 9
  //   X1: pin 14
  //   Data: pin 3
  //   Write: pin 2
  //   RTN: pin 11
  //   JMP: pin 12
  //   RR: pin 15
  //   X2: pin 13
  //   RST: pin 1
endmodule
