// Digital circuit MC14512.dig as structural Verilog
module MC14512 (
  input  A,
  input  B,
  input  C,
  input  INH,
  input  DIS,
  input  X0,
  input  X1,
  input  X2,
  input  X3,
  input  X4,
  input  X5,
  input  X6,
  input  X7,
  output Z
);

  wire and_1_out, multiplexer_1_out, not_1_out, not_2_out;

  not not_1 (not_1_out, INH);
  not not_2 (not_2_out, DIS);
  Multiplexer #(.Selector_Bits(3)) multiplexer_1 (
    .sel({C, B, A}), .in_0(X0), .in_1(X1), .in_2(X2), .in_3(X3), .in_4(X4), .in_5(X5), .in_6(X6), .in_7(X7),
    .out(multiplexer_1_out));
  and and_1 (and_1_out, multiplexer_1_out, not_1_out);
  assign Z = not_2_out ? and_1_out : 1'bz;  // Driver driver_1

  // Notes on the sheet:
  //   A: pin 11
  //   B: pin 12
  //   C: pin 13
  //   INH: pin 10
  //   DIS: pin 15
  //   Z: pin 14
  //   X0: pin 1
  //   X1: pin 2
  //   X2: pin 4
  //   X3: pin 5
  //   X4: pin 5
  //   X5: pin 6
  //   X6: pin 7
  //   X7: pin 9
endmodule
