// Digital circuit MC14599.dig as structural Verilog
module MC14599 (
  input  Data,
  input  RESET,
  input  A0,
  input  A1,
  input  A2,
  input  Enable,
  input  Write,
  input  WriteDisable,
  output Q7,
  output Q6,
  output Q5,
  output Q4,
  output Q3,
  output Q2,
  output Q1,
  output Q0
);

  wire and_1_out, and_2_out, demultiplexer_1_out_0, demultiplexer_1_out_1, demultiplexer_1_out_2,
       demultiplexer_1_out_3, demultiplexer_1_out_4, demultiplexer_1_out_5, demultiplexer_1_out_6,
       demultiplexer_1_out_7, multiplexer_1_out, not_1_out, not_2_out;

  not not_1 (not_1_out, WriteDisable);
  assign Data = and_1_out ? multiplexer_1_out : 1'bz;  // Driver driver_1
  and and_1 (and_1_out, Enable, not_2_out);
  not not_2 (not_2_out, Write);
  and and_2 (and_2_out, Enable, Write, not_1_out);
  Multiplexer #(.Selector_Bits(3)) multiplexer_1 (
    .sel({A2, A1, A0}), .in_0(Q0), .in_1(Q1), .in_2(Q2), .in_3(Q3), .in_4(Q4), .in_5(Q5), .in_6(Q6),
    .in_7(Q7), .out(multiplexer_1_out));
  Demultiplexer #(.Selector_Bits(3)) demultiplexer_1 (
    .sel({A2, A1, A0}), .in(and_2_out), .out_0(demultiplexer_1_out_0), .out_1(demultiplexer_1_out_1),
    .out_2(demultiplexer_1_out_2), .out_3(demultiplexer_1_out_3), .out_4(demultiplexer_1_out_4),
    .out_5(demultiplexer_1_out_5), .out_6(demultiplexer_1_out_6), .out_7(demultiplexer_1_out_7));
  D_FF_AS d_ff_as_1 (.Set(1'b0), .D(Data), .C(demultiplexer_1_out_0), .Clr(RESET), .Q(Q0));  // open: nQ
  D_FF_AS d_ff_as_2 (.Set(1'b0), .D(Data), .C(demultiplexer_1_out_1), .Clr(RESET), .Q(Q1));  // open: nQ
  D_FF_AS d_ff_as_3 (.Set(1'b0), .D(Data), .C(demultiplexer_1_out_2), .Clr(RESET), .Q(Q2));  // open: nQ
  D_FF_AS d_ff_as_4 (.Set(1'b0), .D(Data), .C(demultiplexer_1_out_3), .Clr(RESET), .Q(Q3));  // open: nQ
  D_FF_AS d_ff_as_5 (.Set(1'b0), .D(Data), .C(demultiplexer_1_out_4), .Clr(RESET), .Q(Q4));  // open: nQ
  D_FF_AS d_ff_as_6 (.Set(1'b0), .D(Data), .C(demultiplexer_1_out_5), .Clr(RESET), .Q(Q5));  // open: nQ
  D_FF_AS d_ff_as_7 (.Set(1'b0), .D(Data), .C(demultiplexer_1_out_6), .Clr(RESET), .Q(Q6));  // open: nQ
  D_FF_AS d_ff_as_8 (.Set(1'b0), .D(Data), .C(demultiplexer_1_out_7), .Clr(RESET), .Q(Q7));  // open: nQ
endmodule
