// Logisim project LU_CTL.circ as structural Verilog: 2 circuits, main circuit CTL
module CTL (
  input  [3:0] I,
  output SetRR,
  output NotOut,
  output Write,
  output SetIEN,
  output SetOEN,
  output JMP,
  output RTN,
  output Skip,
  output FLG0,
  output FLGF
);

  wire and_1_out, and_2_out, and_3_out, and_9_out, and_10_out, not_1_out, not_2_out, not_3_out, not_4_out;

  not not_1 (not_1_out, I[3]);
  not not_2 (not_2_out, I[2]);
  not not_3 (not_3_out, I[1]);
  not not_4 (not_4_out, I[0]);
  and and_1 (and_1_out, not_1_out, I[0]);
  and and_2 (and_2_out, not_1_out, I[1]);
  or or_1 (SetRR, and_1_out, and_2_out, and_3_out);
  and and_3 (and_3_out, not_1_out, I[2]);
  and and_4 (Write, I[3], not_2_out, not_3_out);
  and and_5 (SetIEN, I[3], not_2_out, I[1], not_4_out);
  and and_6 (SetOEN, I[3], not_2_out, I[1], I[0]);
  and and_7 (JMP, I[3], I[2], not_3_out, not_4_out);
  and and_8 (RTN, I[3], I[2], not_3_out, I[0]);
  and and_9 (and_9_out, I[3], I[2], not_3_out, I[0]);
  or or_2 (Skip, and_9_out, and_10_out);
  and and_10 (and_10_out, I[3], I[2], I[1], not_4_out);
  and and_11 (FLG0, not_1_out, not_2_out, not_3_out, not_4_out);
  and and_12 (FLGF, I[3], I[2], I[1], I[0]);

  assign NotOut = I[0];
endmodule

module LU (
  input  [2:0] I,
  input  RR,
  input  DIn,
  output NewRR
);

  wire and_1_out, and_2_out, and_3_out, and_4_out, and_5_out, and_6_out, not_1_out, not_2_out, not_3_out,
       not_4_out, not_5_out;

  not not_1 (not_1_out, I[2]);
  not not_2 (not_2_out, I[1]);
  not not_3 (not_3_out, I[0]);
  not not_4 (not_4_out, RR);
  not not_5 (not_5_out, DIn);
  and and_1 (and_1_out, not_1_out, I[0], RR, DIn);
  and and_2 (and_2_out, I[1], not_3_out, not_5_out);
  and and_3 (and_3_out, I[2], I[1], not_3_out, RR);
  and and_4 (and_4_out, I[2], I[0], not_4_out, DIn);
  and and_5 (and_5_out, I[2], RR, not_5_out);
  and and_6 (and_6_out, not_2_out, I[0], DIn);
  or or_1 (NewRR, and_1_out, and_2_out, and_3_out, and_4_out, and_5_out, and_6_out);
endmodule
